# Fritzing sketch mega-wiring (saved by Fritzing 0.9.3b)
breadboards: 1

parts:
  Part1 = Arduino Mega 2560 (Rev3)
  R1 = Resistor [tolerance=±5% resistance=68 power=0.25W package=THT]
  LED1 = LED - 3mm [color="White (6500K)" package="3 mm [THT]"]
  LED2 = LED - 3mm [color="White (6500K)" package="3 mm [THT]"]
  R2 = Resistor [tolerance=±5% resistance=68 power=0.25W package=THT]
  R3 = Resistor [tolerance=±5% resistance=68 power=0.25W package=THT]
  R4 = Resistor [tolerance=±5% resistance=68 power=0.25W package=THT]
  R5 = Resistor [tolerance=±5% resistance=68 power=0.25W package=THT]
  LED3 = LED - 3mm [color="White (6500K)" package="3 mm [THT]"]
  LED4 = LED - 3mm [color="White (6500K)" package="3 mm [THT]"]
  LED5 = LED - 3mm [color="White (6500K)" package="3 mm [THT]"]
  DHT1 = DHT22 Humidity and Temperature Sensor
  Part2 = Soil Moisture Sensor
  Part3 = RFID-RC522-v3
  SW-1 = Vibration sensor module

nets:
  N1: Part1.A0, Part2.SIG
  VCC: Part1.5V, DHT1.VDD, Part2.VCC, Part3.3.3V, SW-1.vcc
  GND: Part1.GND, R1.Pin_0, R2.Pin_0, R3.Pin_0, R4.Pin_0, R5.Pin_0, DHT1.GND, Part2.GND, Part3.GND, SW-1.Ground
  N2: Part1.D2_PWM, LED5.anode
  N3: Part1.D3_PWM, LED4.anode
  N4: Part1.D4_PWM, LED3.anode
  N5: Part1.D5_PWM, LED2.anode
  N6: Part1.D6_PWM, LED1.anode
  N7: Part1.D22, DHT1.DATA
  N8: Part1.D23, SW-1.Digital_output
  N9: Part1.D49, Part3.RST
  N10: Part1.D50, Part3.MISO
  N11: Part1.D51, Part3.MOSI
  N12: Part1.D52, Part3.SCK
  N13: Part1.D53, Part3.SDA
  N14: R1.Pin_1, LED1.cathode
  N15: LED2.cathode, R2.Pin_1
  N16: R3.Pin_1, LED3.cathode
  N17: R4.Pin_1, LED4.cathode
  N18: R5.Pin_1, LED5.cathode

custom parts:
  RFID-RC522-v3: A simple China made RFID-RC522 Reader (6x4 cm); do check the pin labels, as this is a MFRC522 based clone.
  Vibration sensor module: Single-roller type full induction trigger switch. When no vibration or tilt, the product is ON conduction state, and in the steady state, when a vibration or tilt, the switch will be rendered instantly disconnect the conductive resistance increases, generating a current pulse signal, thereby triggering circuit. The default state of the swith is close Digital output Supply voltage:3.3V-5V On-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
